// Logisim project PIPO.circ as structural Verilog: 1 circuit, main circuit main
module main (
  input  PA,
  input  PB,
  input  PC,
  input  PD,
  input  PE,
  input  A,
  input  B
);

  wire CLK_out, CLR_out, d_ff_1_q, d_ff_2_q, d_ff_3_q, d_ff_4_q, d_ff_5_q;

  Clock CLK (.out(CLK_out));
  Button CLR (.out(CLR_out));
  D_Flip_Flop d_ff_1 (.D(PA), .clk(CLK_out), .Q(d_ff_1_q), .Qn(CLR_out));  // open: preset, reset
  // AND_Gate and_1 has open pins: in0=A, in1=B, out=open
  LED led_1 (.in(d_ff_1_q));
  D_Flip_Flop d_ff_2 (.D(PB), .clk(CLK_out), .Q(d_ff_2_q), .Qn(CLR_out));  // open: preset, reset
  D_Flip_Flop d_ff_3 (.D(PC), .clk(CLK_out), .Q(d_ff_3_q), .Qn(CLR_out));  // open: preset, reset
  LED led_2 (.in(d_ff_2_q));
  LED led_3 (.in(d_ff_3_q));
  D_Flip_Flop d_ff_4 (.D(PD), .clk(CLK_out), .Q(d_ff_4_q), .Qn(CLR_out));  // open: preset, reset
  LED led_4 (.in(d_ff_4_q));
  D_Flip_Flop d_ff_5 (.D(PE), .clk(CLK_out), .Q(d_ff_5_q), .Qn(CLR_out));  // open: preset, reset
  LED led_5 (.in(d_ff_5_q));

  // Notes on the sheet:
  //   MSB
  //   5-Bit Parallel Out Shift Register (PIPO)
  //   Bit 1
  //   Bit 2
  //   Bit 3
  //   Bit 4
  //   LSB
  //   Bit 5
endmodule
