// Logisim project SIPO.circ as structural Verilog: 1 circuit, main circuit main
module main (
  input  D
);

  wire CLK_out, CLR_out, d_ff_1_q, d_ff_2_q, d_ff_3_q, d_ff_4_q, d_ff_5_q, d_ff_6_q, d_ff_7_q, d_ff_8_q,
       d_ff_9_q, not_1_out;

  LED CPLED (.in(CLK_out));
  Clock CLK (.out(CLK_out));
  Button CLR (.out(CLR_out));
  not not_1 (not_1_out, CLK_out);
  D_Flip_Flop d_ff_1 (.D(D), .clk(not_1_out), .Q(d_ff_1_q), .reset(CLR_out));  // open: Qn, preset
  LED QA (.in(d_ff_1_q));
  D_Flip_Flop d_ff_2 (.D(d_ff_1_q), .clk(not_1_out), .Q(d_ff_2_q), .reset(CLR_out));  // open: Qn, preset
  LED QB (.in(d_ff_2_q));
  D_Flip_Flop d_ff_3 (.D(d_ff_2_q), .clk(not_1_out), .Q(d_ff_3_q), .reset(CLR_out));  // open: Qn, preset
  LED QC (.in(d_ff_3_q));
  D_Flip_Flop d_ff_4 (.D(d_ff_3_q), .clk(not_1_out), .Q(d_ff_4_q), .reset(CLR_out));  // open: Qn, preset
  LED QD (.in(d_ff_4_q));
  D_Flip_Flop d_ff_5 (.D(d_ff_4_q), .clk(not_1_out), .Q(d_ff_5_q), .reset(CLR_out));  // open: Qn, preset
  LED QE (.in(d_ff_5_q));
  D_Flip_Flop d_ff_6 (.D(d_ff_5_q), .clk(not_1_out), .Q(d_ff_6_q), .reset(CLR_out));  // open: Qn, preset
  LED QF (.in(d_ff_6_q));
  D_Flip_Flop d_ff_7 (.D(d_ff_6_q), .clk(not_1_out), .Q(d_ff_7_q), .reset(CLR_out));  // open: Qn, preset
  LED QG (.in(d_ff_7_q));
  D_Flip_Flop d_ff_8 (.D(d_ff_7_q), .clk(not_1_out), .Q(d_ff_8_q), .reset(CLR_out));  // open: Qn, preset
  LED QH (.in(d_ff_8_q));
  D_Flip_Flop d_ff_9 (.D(d_ff_8_q), .clk(not_1_out), .Q(d_ff_9_q), .reset(CLR_out));  // open: Qn, preset
  LED QI (.in(d_ff_9_q));

  // Notes on the sheet:
  //   MSB
  //   Data Keluar Parallel
  //   9 Bit Serial In Parallel Out Shift Register
  //   LSB
endmodule
