// Logisim project SISO.circ as structural Verilog: 1 circuit, main circuit main
module main (
  input  Serial_In
);

  wire CLK_out, CLR_out, d_ff_1_q, d_ff_2_q, d_ff_3_q, d_ff_4_q, d_ff_5_q, d_ff_6_q, d_ff_7_q, d_ff_8_q;

  D_Flip_Flop d_ff_1 (.D(Serial_In), .clk(CLK_out), .Q(d_ff_1_q), .reset(CLR_out));  // open: Qn, preset
  Clock CLK (.out(CLK_out));
  Button CLR (.out(CLR_out));
  D_Flip_Flop d_ff_2 (.D(d_ff_1_q), .clk(CLK_out), .Q(d_ff_2_q), .reset(CLR_out));  // open: Qn, preset
  D_Flip_Flop d_ff_3 (.D(d_ff_2_q), .clk(CLK_out), .Q(d_ff_3_q), .reset(CLR_out));  // open: Qn, preset
  D_Flip_Flop d_ff_4 (.D(d_ff_3_q), .clk(CLK_out), .Q(d_ff_4_q), .reset(CLR_out));  // open: Qn, preset
  D_Flip_Flop d_ff_5 (.D(d_ff_4_q), .clk(CLK_out), .Q(d_ff_5_q), .reset(CLR_out));  // open: Qn, preset
  D_Flip_Flop d_ff_6 (.D(d_ff_5_q), .clk(CLK_out), .Q(d_ff_6_q), .reset(CLR_out));  // open: Qn, preset
  D_Flip_Flop d_ff_7 (.D(d_ff_6_q), .clk(CLK_out), .Q(d_ff_7_q), .reset(CLR_out));  // open: Qn, preset
  D_Flip_Flop d_ff_8 (.D(d_ff_7_q), .clk(CLK_out), .Q(d_ff_8_q), .reset(CLR_out));  // open: Qn, preset
  LED led_1 (.in(d_ff_8_q));

  // Notes on the sheet:
  //   MSB
  //   8-bit Serial In Serial Out Shift Register 
  //   LSB
  //   Serial Out
endmodule
